# Fritzing sketch clock_back_pcb (saved by Fritzing 0.9.4)
circuit board: 3.9cm x 6.3cm
perfboards: 1

parts:
  Part1 = Arduino Nano (Rev3.0)
  J3 = male pin header, 4 pins [form="♂ (male)"]
  J4 = male pin header, 4 pins [form="♂ (male)"]
  J5 = male pin header, 7 pins [form="♂ (male)"]
  J6 = double row male pin header, 2 pins [form="♂ (male)"]
  J7 = male pin header, 3 pins [form="♂ (male)"]

nets:
  N1: Part1.GND, J5.pin6, J6.pin1
  N2: Part1.D3, J5.pin7
  N3: Part1.D4, J5.pin5
  N4: Part1.D5, J5.pin4
  N5: Part1.D6, J7.pin1
  N6: Part1.D7, J7.pin2
  N7: Part1.D8, J7.pin3
  N8: Part1.D9, J3.pin1
  N9: Part1.D10, J3.pin2
  N10: Part1.D11/MOSI, J3.pin3
  N11: Part1.D12/MISO, J3.pin4
  N12: Part1.5V, J5.pin3, J6.pin2
  N13: Part1.A5, J5.pin2
  N14: Part1.A4, J5.pin1
  N15: Part1.A3, J4.pin1
  N16: Part1.A2, J4.pin2
  N17: Part1.A1, J4.pin3
  N18: Part1.A0, J4.pin4
