# Fritzing sketch mixer_pcb (saved by Fritzing 0.9.4)
circuit board: 4cm x 10cm
perfboards: 1

parts:
  J1 = shrouded pin header, 10 pins [form="♂ (shrouded male)"]
  B100k = Potentiometer
  B100k_2 = Potentiometer
  B100k_3 = Potentiometer
  B100k_4 = Potentiometer
  S2 = Toggle Switch [package=THT]
  3_5mm2 = 3.5mm verticle mono jack
  S1 = Toggle Switch [package=THT]
  3_5mm1 = 3.5mm verticle mono jack
  R5 = Resistor [tolerance=±5% resistance=100k package=THT]
  R8 = Resistor [tolerance=±5% resistance=100k package=THT]
  S3 = Toggle Switch [package=THT]
  3_5mm3 = 3.5mm verticle mono jack
  R14 = Resistor [tolerance=±5% resistance=470 package=THT]
  S4 = Toggle Switch [package=THT]
  3_5mm4 = 3.5mm verticle mono jack
  R6 = Resistor [tolerance=±5% resistance=100k package=THT]
  R7 = Resistor [tolerance=±5% resistance=100k package=THT]
  3_5mm5 = 3.5mm verticle mono jack
  S5 = Toggle Switch [package=THT]
  3_5mm6 = 3.5mm verticle mono jack
  R13 = Resistor [tolerance=±5% resistance=1k package=THT]
  R10 = Resistor [tolerance=±5% resistance=100k package=THT]
  R9 = Resistor [tolerance=±5% resistance=100k package=THT]
  R12 = Resistor [tolerance=±5% resistance=100k package=THT]
  R11 = Resistor [tolerance=±5% resistance=100k package=THT]
  LED = LED - 3mm [color="Red (633nm)" package="3 mm [THT]"]
  IC1 = IC, DIP package, 8 pins [chip_label=TL072]
  C1 = Electrolytic Capacitor [capacitance=10µF package="100 mil [THT, electrolytic]"]
  C2 = Electrolytic Capacitor [capacitance=10µF package="100 mil [THT, electrolytic]"]
  C3 = Ceramic Capacitor [capacitance=100nF package="100 mil [THT, multilayer]"]
  C4 = Ceramic Capacitor [capacitance=100nF package="100 mil [THT, multilayer]"]

nets:
  N1: J1.pin1, J1.pin10, IC1.pin4, C2.-, C3.0
  N2: J1.pin2, J1.pin3, J1.pin4, J1.pin7, J1.pin8, J1.pin9, B100k.CCW, B100k.Chassis#4, B100k_2.CCW, B100k_2.Chassis, B100k_3.CCW, B100k_3.Chassis, B100k_4.CCW, B100k_4.Chassis#3, S2.L1, 3_5mm2.Shank, 3_5mm2.Switch, S1.L1, 3_5mm1.Shank, 3_5mm1.Switch, S3.L1, 3_5mm3.Shank, R14.Pin_0, S4.L1, 3_5mm4.Shank, 3_5mm4.Switch, 3_5mm5.Shank, 3_5mm5.Switch, IC1.pin3, IC1.pin5, C1.-, C2.+, C3.1, C4.1
  N3: J1.pin5, J1.pin6, IC1.pin8, C1.+, C4.0
  N4: B100k.WIPER, R5.Pin_0
  N5: B100k.CW, S1.COM
  N6: B100k_2.WIPER, R6.Pin_0
  N7: B100k_2.CW, S2.COM
  N8: B100k_3.WIPER, R7.Pin_0
  N9: B100k_3.CW, S3.COM
  N10: B100k_4.WIPER, R8.Pin_0
  N11: B100k_4.CW, S4.COM
  N12: S2.L2, 3_5mm2.Tip
  N13: S1.L2, 3_5mm1.Tip
  N14: R5.Pin_1, R8.Pin_1, R6.Pin_1, R7.Pin_1, R10.Pin_0, R9.Pin_1, IC1.pin2
  N15: S3.L2, 3_5mm3.Tip
  N16: R14.Pin_1, S5.L1, 3_5mm6.Shank, LED.anode
  N17: S4.L2, 3_5mm4.Tip
  N18: 3_5mm5.Tip, S5.L2
  N19: S5.COM, R9.Pin_0
  N20: 3_5mm6.Tip, R13.Pin_1
  N21: R13.Pin_0, R12.Pin_0, R11.Pin_1, IC1.pin7
  N22: R10.Pin_1, R11.Pin_0, LED.cathode, IC1.pin1
  N23: R12.Pin_1, IC1.pin6

notes:
  -12v
  Mixer v0.1
  --

custom parts:
  Potentiometer: Modular Addict 9mm vertical potentiometer
  3.5mm verticle mono jack: Thonkiconn pj301m-12 verticle mono switched 3.5mm jack.
