# Fritzing sketch rng_front (saved by Fritzing 0.9.4)
circuit board: 4.9cm x 10cm
perfboards: 1

parts:
  LED2 = LED - 5mm [color="Red (633nm)" package="5 mm [THT]"]
  LED3 = LED - 5mm [color="Red (633nm)" package="5 mm [THT]"]
  LED4 = LED - 5mm [color="Red (633nm)" package="5 mm [THT]"]
  LED5 = LED - 5mm [color="Red (633nm)" package="5 mm [THT]"]
  LED7 = LED - 5mm [color="Red (633nm)" package="5 mm [THT]"]
  R11 = Resistor [tolerance=±5% resistance=1k package=THT]
  R12 = Resistor [tolerance=±5% resistance=1k package=THT]
  R13 = Resistor [tolerance=±5% resistance=1k package=THT]
  R14 = Resistor [tolerance=±5% resistance=10k package=THT]
  R15 = Resistor [tolerance=±5% resistance=10k package=THT]
  R16 = Resistor [tolerance=±5% resistance=220 package=THT]
  R17 = Resistor [tolerance=±5% resistance=220 package=THT]
  LED1 = LED - 5mm [color="Red (633nm)" package="5 mm [THT]"]
  LED6 = LED - 5mm [color="Red (633nm)" package="5 mm [THT]"]
  LED8 = LED - 3mm [color="Red (633nm)" package="3 mm [THT]"]
  LED9 = LED - 3mm [color="Red (633nm)" package="3 mm [THT]"]
  Encoder1 = Rotary encoder with push button
  R2 = Potentiometer
  R1 = Potentiometer
  R3 = Potentiometer
  3_5mm1 = 3.5mm verticle mono jack
  3_5mm4 = 3.5mm verticle mono jack
  3_5mm5 = 3.5mm verticle mono jack
  3_5mm6 = 3.5mm verticle mono jack
  3_5mm3 = 3.5mm verticle mono jack
  3_5mm2 = 3.5mm verticle mono jack
  S2 = Toggle Switch [package=THT]
  S1 = Toggle Switch [package=THT]
  J4 = male pin header, 8 pins [form="♂ (male)"]
  J5 = male pin header, 4 pins [form="♂ (male)"]
  J1 = male pin header, 7 pins [form="♂ (male)"]
  J8 = male pin header, 5 pins [form="♂ (male)"]

nets:
  N1: LED2.cathode, J1.pin2
  N2: LED2.anode, LED3.anode, LED4.anode, LED5.anode, LED7.anode, LED1.anode, LED6.anode, R2.CW, R1.CW, R3.CW, S2.L2, J4.pin2
  N3: LED3.cathode, J1.pin3
  N4: LED4.cathode, J1.pin4
  N5: LED5.cathode, J1.pin5
  N6: LED7.cathode, J1.pin7
  N7: R11.Pin_0, J5.pin3
  N8: R11.Pin_1, 3_5mm1.Tip
  N9: R12.Pin_0, J4.pin8
  N10: R12.Pin_1, 3_5mm5.Tip
  N11: R13.Pin_0, J4.pin7
  N12: R13.Pin_1, 3_5mm6.Tip
  N13: R14.Pin_0, R16.Pin_1, J8.pin1
  N14: R14.Pin_1, 3_5mm4.Tip
  N15: R15.Pin_0, R17.Pin_1, J8.pin2
  N16: R15.Pin_1, 3_5mm3.Tip
  N17: R16.Pin_0, LED8.anode
  N18: R17.Pin_0, LED9.anode
  N19: LED1.cathode, J1.pin1
  N20: LED6.cathode, J1.pin6
  GND: LED8.cathode, LED9.cathode, Encoder1.COM, Encoder1.SPST1B, R2.CCW, R2.Chassis#3, R1.CCW, R1.Chassis#3, R3.CCW, R3.Chassis, 3_5mm1.Shank, 3_5mm1.Switch, 3_5mm4.Shank, 3_5mm5.Shank, 3_5mm5.Switch, 3_5mm6.Shank, 3_5mm6.Switch, 3_5mm3.Shank, 3_5mm2.Shank, S2.L1, J4.pin1
  N21: Encoder1.Encoder_A, J5.pin2
  N22: Encoder1.Encoder_B, J5.pin1
  N23: Encoder1.SPST1A, J4.pin4
  N24: R2.WIPER, J4.pin6
  N25: R1.WIPER, J4.pin3
  N26: R3.WIPER, J4.pin5
  N27: 3_5mm2.Tip, J8.pin3
  N28: S2.COM, J5.pin4
  N29: S1.L1, J8.pin5
  N30: S1.COM, J8.pin4

notes:
  RNG front v0.5

custom parts:
  Potentiometer: Modular Addict 9mm vertical potentiometer
  3.5mm verticle mono jack: Thonkiconn pj301m-12 verticle mono switched 3.5mm jack.
