# Fritzing sketch rng_front (saved by Fritzing 0.9.4)
circuit board: 4.9cm x 10cm
perfboards: 1

parts:
  LED2 = LED - 5mm [color="Red (633nm)" package="5 mm [THT]"]
  LED3 = LED - 5mm [color="Red (633nm)" package="5 mm [THT]"]
  LED4 = LED - 5mm [color="Red (633nm)" package="5 mm [THT]"]
  LED5 = LED - 5mm [color="Red (633nm)" package="5 mm [THT]"]
  LED7 = LED - 5mm [color="Red (633nm)" package="5 mm [THT]"]
  R4 = Resistor [tolerance=±5% resistance=220 package=THT]
  R5 = Resistor [tolerance=±5% resistance=220 package=THT]
  R6 = Resistor [tolerance=±5% resistance=220 package=THT]
  R7 = Resistor [tolerance=±5% resistance=220 package=THT]
  R8 = Resistor [tolerance=±5% resistance=220 package=THT]
  R9 = Resistor [tolerance=±5% resistance=220 package=THT]
  R10 = Resistor [tolerance=±5% resistance=220 package=THT]
  J1 = male pin header, 7 pins [form="♂ (male)"]
  J8 = male pin header, 5 pins [form="♂ (male)"]
  J5 = male pin header, 4 pins [form="♂ (male)"]
  R11 = Resistor [tolerance=±5% resistance=1k package=THT]
  R12 = Resistor [tolerance=±5% resistance=1k package=THT]
  R13 = Resistor [tolerance=±5% resistance=1k package=THT]
  R14 = Resistor [tolerance=±5% resistance=10k package=THT]
  R15 = Resistor [tolerance=±5% resistance=10k package=THT]
  R16 = Resistor [tolerance=±5% resistance=220 package=THT]
  R17 = Resistor [tolerance=±5% resistance=220 package=THT]
  J4 = male pin header, 8 pins [form="♂ (male)"]
  LED1 = LED - 5mm [color="Red (633nm)" package="5 mm [THT]"]
  LED6 = LED - 5mm [color="Red (633nm)" package="5 mm [THT]"]
  LED8 = LED - 3mm [color="Red (633nm)" package="3 mm [THT]"]
  LED9 = LED - 3mm [color="Red (633nm)" package="3 mm [THT]"]
  Encoder1 = Rotary encoder with push button
  R2 = Potentiometer
  R1 = Potentiometer
  R3 = Potentiometer
  3_5mm1 = 3.5mm verticle mono jack
  3_5mm4 = 3.5mm verticle mono jack
  3_5mm5 = 3.5mm verticle mono jack
  3_5mm6 = 3.5mm verticle mono jack
  3_5mm3 = 3.5mm verticle mono jack
  S3 = Toggle Switch [package=THT]
  S4 = Toggle Switch [package=THT]
  3_5mm2 = 3.5mm verticle mono jack

nets:
  N1: LED2.cathode, J1.pin2
  N2: LED2.anode, R9.Pin_1
  N3: LED3.cathode, J1.pin3
  N4: LED3.anode, R8.Pin_1
  N5: LED4.cathode, J1.pin4
  N6: LED4.anode, R7.Pin_1
  N7: LED5.cathode, J1.pin5
  N8: LED5.anode, R6.Pin_1
  N9: LED7.cathode, J1.pin7
  N10: LED7.anode, R4.Pin_1
  N11: R4.Pin_0, R5.Pin_0, R6.Pin_0, R7.Pin_0, R8.Pin_0, R9.Pin_0, R10.Pin_0, J4.pin2, R2.CW, R1.CW, R3.CW, S4.L2
  N12: R5.Pin_1, LED6.anode
  N13: R10.Pin_1, LED1.anode
  N14: J1.pin1, LED1.cathode
  N15: J1.pin6, LED6.cathode
  N16: J8.pin1, R14.Pin_0, R16.Pin_1
  N17: J8.pin2, R15.Pin_0, R17.Pin_1
  N18: J8.pin3, 3_5mm2.Tip
  N19: J8.pin4, S3.COM
  N20: J8.pin5, S3.L1
  N21: J5.pin1, Encoder1.Encoder_B
  N22: J5.pin2, Encoder1.Encoder_A
  N23: J5.pin3, R11.Pin_0
  N24: J5.pin4, S4.COM
  N25: R11.Pin_1, 3_5mm1.Tip
  N26: R12.Pin_0, J4.pin8
  N27: R12.Pin_1, 3_5mm5.Tip
  N28: R13.Pin_0, J4.pin7
  N29: R13.Pin_1, 3_5mm6.Tip
  N30: R14.Pin_1, 3_5mm4.Tip
  N31: R15.Pin_1, 3_5mm3.Tip
  N32: R16.Pin_0, LED8.anode
  N33: R17.Pin_0, LED9.anode
  GND: J4.pin1, LED8.cathode, LED9.cathode, Encoder1.COM, Encoder1.SPST1B, R2.CCW, R2.Chassis#3, R1.CCW, R1.Chassis#3, R3.CCW, R3.Chassis#3, 3_5mm1.Shank, 3_5mm1.Switch, 3_5mm4.Shank, 3_5mm5.Shank, 3_5mm5.Switch, 3_5mm6.Shank, 3_5mm6.Switch, 3_5mm3.Shank, S4.L1, 3_5mm2.Shank
  N34: J4.pin3, R1.WIPER
  N35: J4.pin4, Encoder1.SPST1A
  N36: J4.pin5, R3.WIPER
  N37: J4.pin6, R2.WIPER

custom parts:
  Potentiometer: Modular Addict 9mm vertical potentiometer
  3.5mm verticle mono jack: Thonkiconn pj301m-12 verticle mono switched 3.5mm jack.
