# Fritzing sketch rng_front (saved by Fritzing 0.9.4)
perfboards: 1

parts:
  R1 = Potentiometer
  R2 = Potentiometer
  R3 = Potentiometer
  Encoder1 = Rotary encoder with push button
  S1 = Toggle Switch [package=THT]  # not connected
  S2 = Toggle Switch [package=THT]
  3_5mm1 = 3.5mm verticle mono jack
  3_5mm2 = 3.5mm verticle mono jack
  3_5mm3 = 3.5mm verticle mono jack
  3_5mm4 = 3.5mm verticle mono jack
  3_5mm5 = 3.5mm verticle mono jack
  3_5mm6 = 3.5mm verticle mono jack
  LED1 = LED - 5mm [color="Red (633nm)" package="5 mm [THT]"]
  LED2 = LED - 5mm [color="Red (633nm)" package="5 mm [THT]"]
  LED3 = LED - 5mm [color="Red (633nm)" package="5 mm [THT]"]
  LED4 = LED - 5mm [color="Red (633nm)" package="5 mm [THT]"]
  LED5 = LED - 5mm [color="Red (633nm)" package="5 mm [THT]"]
  LED6 = LED - 5mm [color="Red (633nm)" package="5 mm [THT]"]
  LED7 = LED - 5mm [color="Red (633nm)" package="5 mm [THT]"]
  R4 = Resistor [tolerance=±5% resistance=220 package=THT]
  R5 = Resistor [tolerance=±5% resistance=220 package=THT]
  R6 = Resistor [tolerance=±5% resistance=220 package=THT]
  R7 = Resistor [tolerance=±5% resistance=220 package=THT]
  R8 = Resistor [tolerance=±5% resistance=220 package=THT]
  R9 = Resistor [tolerance=±5% resistance=220 package=THT]
  R10 = Resistor [tolerance=±5% resistance=220 package=THT]
  J1 = male pin header, 7 pins [form="♂ (male)"]
  J4 = male pin header, 9 pins [form="♂ (male)"]

nets:
  N1: R1.CCW, R2.CCW
  N2: R1.WIPER, J4.pin4
  N3: R1.CW, R2.CW, R4.Pin_0, R5.Pin_0, R6.Pin_0, R7.Pin_0, R8.Pin_0, R9.Pin_0, R10.Pin_0
  N4: R2.WIPER, J4.pin5
  N5: R3.CCW, Encoder1.COM, Encoder1.SPST1B, S2.L1, 3_5mm1.Shank, 3_5mm2.Shank, 3_5mm3.Shank, 3_5mm4.Shank, 3_5mm5.Shank, 3_5mm6.Shank
  N6: R3.CW, S2.L2
  N7: Encoder1.Encoder_A, J4.pin8
  N8: Encoder1.Encoder_B, J4.pin9
  N9: Encoder1.SPST1A, J4.pin7
  N10: LED1.cathode, J1.pin1
  N11: LED1.anode, R10.Pin_1
  N12: LED2.cathode, J1.pin2
  N13: LED2.anode, R9.Pin_1
  N14: LED3.cathode, J1.pin3
  N15: LED3.anode, R8.Pin_1
  N16: LED4.cathode, J1.pin4
  N17: LED4.anode, R7.Pin_1
  N18: LED5.cathode, J1.pin5
  N19: LED5.anode, R6.Pin_1
  N20: LED6.cathode, J1.pin6
  N21: LED6.anode, R5.Pin_1
  N22: LED7.cathode, J1.pin7
  N23: LED7.anode, R4.Pin_1

custom parts:
  Potentiometer: Modular Addict 9mm vertical potentiometer
  3.5mm verticle mono jack: Thonkiconn pj301m-12 verticle mono switched 3.5mm jack.
