# Fritzing sketch sequencer_pcb_front (saved by Fritzing 0.9.4)
perfboards: 1

parts:
  R1 = Potentiometer
  R2 = Potentiometer
  R3 = Potentiometer
  R4 = Potentiometer
  R5 = Potentiometer
  R6 = Potentiometer
  R7 = Potentiometer
  R8 = Potentiometer
  R9 = Potentiometer
  R10 = Potentiometer
  R11 = Potentiometer
  R12 = Potentiometer
  R13 = Potentiometer
  R14 = Potentiometer
  R15 = Potentiometer
  R16 = Potentiometer
  3_5mm1 = 3.5mm verticle mono jack
  3_5mm2 = 3.5mm verticle mono jack
  3_5mm3 = 3.5mm verticle mono jack
  3_5mm4 = 3.5mm verticle mono jack
  3_5mm5 = 3.5mm verticle mono jack
  3_5mm6 = 3.5mm verticle mono jack
  3_5mm7 = 3.5mm verticle mono jack
  3_5mm8 = 3.5mm verticle mono jack
  3_5mm9 = 3.5mm verticle mono jack
  3_5mm10 = 3.5mm verticle mono jack
  3_5mm11 = 3.5mm verticle mono jack
  3_5mm12 = 3.5mm verticle mono jack
  3_5mm13 = 3.5mm verticle mono jack
  3_5mm14 = 3.5mm verticle mono jack
  3_5mm15 = 3.5mm verticle mono jack
  3_5mm16 = 3.5mm verticle mono jack
  3_5mm17 = 3.5mm verticle mono jack
  LED1 = LED - 3mm [color="Red (633nm)" package="3 mm [THT]"]
  LED2 = LED - 3mm [color="Red (633nm)" package="3 mm [THT]"]
  LED3 = LED - 3mm [color="Red (633nm)" package="3 mm [THT]"]
  LED4 = LED - 3mm [color="Red (633nm)" package="3 mm [THT]"]
  LED5 = LED - 3mm [color="Red (633nm)" package="3 mm [THT]"]
  LED6 = LED - 3mm [color="Red (633nm)" package="3 mm [THT]"]
  LED7 = LED - 3mm [color="Red (633nm)" package="3 mm [THT]"]
  LED8 = LED - 3mm [color="Red (633nm)" package="3 mm [THT]"]
  LED9 = LED - 3mm [color="Red (633nm)" package="3 mm [THT]"]
  LED10 = LED - 3mm [color="Red (633nm)" package="3 mm [THT]"]
  LED11 = LED - 3mm [color="Red (633nm)" package="3 mm [THT]"]
  LED12 = LED - 3mm [color="Red (633nm)" package="3 mm [THT]"]
  LED13 = LED - 3mm [color="Red (633nm)" package="3 mm [THT]"]
  LED14 = LED - 3mm [color="Red (633nm)" package="3 mm [THT]"]
  LED15 = LED - 3mm [color="Red (633nm)" package="3 mm [THT]"]
  LED16 = LED - 3mm [color="Red (633nm)" package="3 mm [THT]"]
  J1 = female pin header, 4 pins [form="♀ (female)"]
  J3 = female pin header, 4 pins [form="♀ (female)"]
  J6 = female pin header, 4 pins [form="♀ (female)"]
  J8 = male pin header, 2 pins [form="♂ (male)"]
  J7 = male pin header, 2 pins [form="♂ (male)"]
  J10 = male pin header, 2 pins [form="♂ (male)"]
  J9 = male pin header, 2 pins [form="♂ (male)"]
  LED17 = LED - 3mm [color="Red (633nm)" package="3 mm [THT]"]
  R19 = Resistor [tolerance=±5% resistance=220 package=THT]
  R20 = Resistor [tolerance=±5% resistance=220 package=THT]
  LED18 = LED - 3mm [color="Red (633nm)" package="3 mm [THT]"]
  R21 = Resistor [tolerance=±5% resistance=220 package=THT]
  R22 = Resistor [tolerance=±5% resistance=220 package=THT]
  LED19 = LED - 3mm [color="Red (633nm)" package="3 mm [THT]"]
  R23 = Resistor [tolerance=±5% resistance=220 package=THT]
  R24 = Resistor [tolerance=±5% resistance=220 package=THT]
  LED20 = LED - 3mm [color="Red (633nm)" package="3 mm [THT]"]
  R25 = Resistor [tolerance=±5% resistance=220 package=THT]
  R26 = Resistor [tolerance=±5% resistance=220 package=THT]
  J13 = female pin header, 4 pins [form="♀ (female)"]
  J14 = female pin header, 4 pins [form="♀ (female)"]
  J5 = female pin header, 10 pins [form="♀ (female)"]
  J4 = female pin header, 7 pins [form="♀ (female)"]
  J2 = female pin header, 6 pins [form="♀ (female)"]

nets:
  N1: R1.CCW, R2.CCW, R3.CCW, R4.CCW, R5.CCW, R6.CCW, R7.CCW, R8.CCW, R9.CCW, R10.CCW, R11.CCW, R12.CCW, R13.CCW, R14.CCW, R15.CCW, R16.CCW, 3_5mm1.Shank, 3_5mm2.Shank, 3_5mm3.Shank, 3_5mm4.Shank, 3_5mm6.Shank, 3_5mm8.Shank, 3_5mm9.Shank, 3_5mm10.Shank, 3_5mm11.Shank, 3_5mm12.Shank, 3_5mm13.Shank, 3_5mm14.Shank, 3_5mm15.Shank, 3_5mm16.Shank, 3_5mm17.Shank, J8.pin1, J7.pin1, J10.pin1, J9.pin1, LED17.cathode, LED18.cathode, LED19.cathode, J5.pin10
  N2: R1.WIPER, J1.pin4
  N3: R1.CW, R2.CW, R3.CW, R4.CW, R5.CW, R6.CW, R7.CW, R8.CW, R9.CW, R10.CW, R11.CW, R12.CW, R13.CW, R14.CW, R15.CW, R16.CW, J5.pin1
  N4: R2.WIPER, J1.pin3
  N5: R3.WIPER, J1.pin1
  N6: R4.WIPER, J1.pin2
  N7: R5.WIPER, J2.pin3
  N8: R6.WIPER, J2.pin2
  N9: R7.WIPER, J2.pin4
  N10: R8.WIPER, J2.pin5
  N11: R9.WIPER, J3.pin2
  N12: R10.WIPER, J3.pin1
  N13: R11.WIPER, J3.pin3
  N14: R12.WIPER, J3.pin4
  N15: R13.WIPER, J4.pin4
  N16: R14.WIPER, J4.pin3
  N17: R15.WIPER, J4.pin5
  N18: R16.WIPER, J4.pin6
  N19: 3_5mm1.Tip, 3_5mm2.Switch, 3_5mm3.Switch, J6.pin4
  N20: 3_5mm2.Tip, J6.pin3
  N21: 3_5mm3.Tip, 3_5mm4.Switch, J6.pin2
  N22: 3_5mm4.Tip, J6.pin1
  N23: 3_5mm5.Shank, 3_5mm7.Shank, LED20.cathode
  N24: 3_5mm5.Tip, R23.Pin_1
  N25: 3_5mm6.Tip, R20.Pin_1
  N26: 3_5mm7.Tip, R25.Pin_1
  N27: 3_5mm8.Tip, R21.Pin_1
  N28: 3_5mm9.Tip, J7.pin2, J2.pin6
  N29: 3_5mm10.Tip, J8.pin2, J2.pin1
  N30: 3_5mm11.Tip, J10.pin2, J4.pin2
  N31: 3_5mm12.Tip, J9.pin2, J4.pin7
  N32: 3_5mm13.Tip, J13.pin2
  N33: 3_5mm14.Tip, J13.pin4
  N34: 3_5mm15.Tip, J13.pin1
  N35: 3_5mm16.Tip, J13.pin3
  N36: 3_5mm17.Tip, J4.pin1
  N37: LED1.cathode, LED2.cathode, LED3.cathode, LED4.cathode, J5.pin2
  N38: LED1.anode, LED8.anode, LED12.anode, LED16.anode, J5.pin3
  N39: LED2.anode, LED7.anode, LED11.anode, LED15.anode, J5.pin5
  N40: LED3.anode, LED5.anode, LED9.anode, LED13.anode, J5.pin7
  N41: LED4.anode, LED6.anode, LED10.anode, LED14.anode, J5.pin9
  N42: LED5.cathode, LED6.cathode, LED7.cathode, LED8.cathode, J5.pin4
  N43: LED9.cathode, LED10.cathode, LED11.cathode, LED12.cathode, J5.pin6
  N44: LED13.cathode, LED14.cathode, LED15.cathode, LED16.cathode, J5.pin8
  N45: LED17.anode, R19.Pin_1
  N46: R19.Pin_0, R20.Pin_0, J14.pin2
  N47: LED18.anode, R22.Pin_1
  N48: R21.Pin_0, R22.Pin_0, J14.pin1
  N49: LED19.anode, R24.Pin_1
  N50: R23.Pin_0, R24.Pin_0, J14.pin3
  N51: LED20.anode, R26.Pin_1
  N52: R25.Pin_0, R26.Pin_0, J14.pin4

custom parts:
  Potentiometer: Modular Addict 9mm vertical potentiometer
  3.5mm verticle mono jack: Thonkiconn pj301m-12 verticle mono switched 3.5mm jack.
